// Digital circuit tp1 compuertas.dig as structural Verilog
module tp1_compuertas (
  input  j,
  input  k,
  input  l
);

  wire and_1_out, and_2_out, and_3_out, and_4_out, and_5_out, and_6_out, and_7_out, and_8_out, and_9_out,
       and_10_out, and_11_out, and_12_out, and_13_out, and_14_out, and_15_out, and_16_out, not_1_out,
       not_2_out, not_3_out, or_1_out, or_2_out, or_3_out, or_4_out, or_5_out, or_6_out, or_7_out, or_8_out;

  not not_1 (not_1_out, j);
  not not_2 (not_2_out, k);
  not not_3 (not_3_out, l);
  or or_1 (or_1_out, not_2_out, not_3_out);
  and and_1 (and_1_out, j, not_2_out);
  and and_2 (and_2_out, k, not_3_out);
  and and_3 (and_3_out, not_2_out, l);
  and and_4 (and_4_out, not_2_out, not_3_out);
  and and_5 (and_5_out, j, not_3_out);
  and and_6 (and_6_out, j, not_2_out);
  or or_2 (or_2_out, and_1_out, and_2_out, and_3_out);
  or or_3 (or_3_out, and_4_out, and_5_out, and_6_out);
  and and_7 (and_7_out, j, not_2_out);
  and and_8 (and_8_out, k, not_3_out);
  and and_9 (and_9_out, not_1_out, not_3_out);
  and and_10 (and_10_out, j, not_2_out);
  and and_11 (and_11_out, not_1_out, not_3_out);
  and and_12 (and_12_out, j, not_2_out, l);
  and and_13 (and_13_out, not_1_out, not_2_out, l);
  and and_14 (and_14_out, j, k, not_3_out);
  and and_15 (and_15_out, not_1_out, not_2_out);
  and and_16 (and_16_out, j, k, not_3_out);
  or or_4 (or_4_out, and_7_out, and_8_out);
  or or_5 (or_5_out, and_9_out, and_10_out);
  or or_6 (or_6_out, and_11_out, and_12_out);
  or or_7 (or_7_out, and_13_out, and_14_out);
  or or_8 (or_8_out, and_15_out, and_16_out);
  Seven_Seg seven_seg_1 (
    .a(or_1_out), .b(1'b0), .c(or_1_out), .d(or_1_out), .e(or_2_out), .f(or_1_out), .g(or_1_out),
    .dp(or_1_out));
  Seven_Seg seven_seg_2 (
    .a(or_5_out), .b(or_8_out), .c(or_7_out), .d(or_6_out), .e(or_5_out), .f(or_4_out), .g(or_3_out),
    .dp(or_1_out));
endmodule
